// Logisim project CastillejoBravo_Paula-sesion1.circ as structural Verilog: 2 circuits, main circuit main
module main (
  input  in_1,
  input  C,
  input  in_3,
  output out_4,
  output out_5
);

  PRACTICA1 practica1_1 (.A(in_1), .B(C), .C(in_3), .X(out_4), .Y(out_5));
endmodule

module PRACTICA1 (
  input  A,
  input  B,
  input  C,
  output X,
  output Y
);

  wire not_1_out;

  not not_1 (not_1_out, A);
  or or_1 (Y, B, C);
  and and_1 (X, not_1_out, Y);
endmodule
