// Logisim project CastillejoBravo_Paula-sesion10.circ as structural Verilog: 1 circuit, main circuit Cuenta atrás Talavera
module \Cuenta_atrás_Talavera  (
);

  wire and_1_out, and_2_out, button_1_out, button_2_out, button_3_out, button_4_out, button_5_out,
       button_6_out, clock_1_out, comparator_1_eq, comparator_1_gt, j_k_ff_1_qn, j_k_ff_2_qn;
  wire [2:0] j_k_ff_1_q;

  Clock clock_1 (.out(clock_1_out));
  J_K_Flip_Flop j_k_ff_1 (
    .J(1'b1), .clk(clock_1_out), .K(1'b1), .Q(j_k_ff_1_q[0]), .Qn(j_k_ff_1_qn), .preset(button_2_out),
    .en(1'b1), .reset(button_1_out));
  Button button_1 (.out(button_1_out));
  Button button_2 (.out(button_2_out));
  Button button_3 (.out(button_3_out));
  J_K_Flip_Flop j_k_ff_2 (
    .J(and_1_out), .clk(clock_1_out), .K(j_k_ff_1_qn), .Q(j_k_ff_1_q[1]), .Qn(j_k_ff_2_qn),
    .preset(button_3_out), .en(1'b1), .reset(button_4_out));
  Button button_4 (.out(button_4_out));
  and and_1 (and_1_out, j_k_ff_1_q[2], j_k_ff_1_qn);
  and and_2 (and_2_out, j_k_ff_1_qn, j_k_ff_2_qn);
  Button button_5 (.out(button_5_out));
  J_K_Flip_Flop j_k_ff_3 (
    .J(and_2_out), .clk(clock_1_out), .K(j_k_ff_1_qn), .Q(j_k_ff_1_q[2]), .preset(button_5_out), .en(1'b1),
    .reset(button_6_out));  // open: Qn
  Button button_6 (.out(button_6_out));
  Hex_Digit_Display hex_digit_display_1 (.value({1'b0, j_k_ff_1_q}));  // open: dp
  LED led_1 (.in(comparator_1_gt));
  LED led_2 (.in(comparator_1_eq));
  Comparator #(.width(4)) comparator_1 (
    .a({1'b0, j_k_ff_1_q}), .b(4'b0000), .gt(comparator_1_gt), .eq(comparator_1_eq));  // open: lt
endmodule
