// Logisim project CastillejoBravo_Paula-sesion11.circ as structural Verilog: 1 circuit, main circuit main
module main (
  input  E
);

  wire and_1_out, and_2_out, decoder_1_out0, decoder_1_out1, decoder_1_out2, decoder_1_out3, decoder_1_out4,
       decoder_1_out5, decoder_1_out6, decoder_1_out7, decoder_1_out8, decoder_1_out9, decoder_1_out10,
       decoder_1_out11, decoder_1_out12, decoder_1_out13, decoder_1_out14, decoder_1_out15,
       multiplexer_1_out, multiplexer_2_out, nor_1_out, not_1_out, not_11_out, not_12_out, not_14_out,
       not_15_out, Reloj_out, Reset_out, xor_1_out;
  wire [0:0] t_ff_1_q;
  wire [1:0] j_k_ff_1_q;

  Clock Reloj (.out(Reloj_out));
  Button Reset (.out(Reset_out));
  nor nor_1 (nor_1_out, j_k_ff_1_q[1], j_k_ff_1_q[0]);
  not not_1 (not_1_out, j_k_ff_1_q[0]);
  xor xor_1 (xor_1_out, j_k_ff_1_q[0], j_k_ff_1_q[1]);
  Multiplexer #(.select(2), .enable("false")) multiplexer_1 (
    .in0(nor_1_out), .in1(not_1_out), .in2(j_k_ff_1_q[0]), .in3(1'b1), .out(multiplexer_1_out),
    .sel({E, t_ff_1_q[0]}));
  Hex_Digit_Display hex_digit_display_1 (.value({1'b0, t_ff_1_q[0], j_k_ff_1_q}));  // open: dp
  T_Flip_Flop t_ff_1 (
    .clk(Reloj_out), .T(multiplexer_1_out), .Q(t_ff_1_q[0]), .reset(Reset_out), .en(1'b1));  // open: Qn, preset
  Multiplexer #(.select(2), .enable("false")) multiplexer_2 (
    .in0(xor_1_out), .in1(1'b0), .in2(1'b0), .in3(1'b1), .out(multiplexer_2_out), .sel({E, t_ff_1_q[0]}));
  LED Q2 (.in(t_ff_1_q[0]));
  D_Flip_Flop d_ff_1 (
    .clk(Reloj_out), .D(multiplexer_2_out), .Q(j_k_ff_1_q[1]), .en(1'b1), .reset(Reset_out));  // open: Qn, preset
  Decoder #(.select(4), .enable("false")) decoder_1 (
    .out0(decoder_1_out0), .out1(decoder_1_out1), .out2(decoder_1_out2), .out3(decoder_1_out3),
    .out4(decoder_1_out4), .out5(decoder_1_out5), .out6(decoder_1_out6), .out7(decoder_1_out7),
    .out8(decoder_1_out8), .out9(decoder_1_out9), .out10(decoder_1_out10), .out11(decoder_1_out11),
    .out12(decoder_1_out12), .out13(decoder_1_out13), .out14(decoder_1_out14), .out15(decoder_1_out15),
    .sel({E, t_ff_1_q[0], j_k_ff_1_q}));
  LED Q1 (.in(j_k_ff_1_q[1]));
  // NOT_Gate not_2 has open pins: in=decoder_1_out0, out=open
  // NOT_Gate not_3 has open pins: in=decoder_1_out1, out=open
  // NOT_Gate not_4 has open pins: in=decoder_1_out2, out=open
  // NOT_Gate not_5 has open pins: in=decoder_1_out3, out=open
  // NOT_Gate not_6 has open pins: in=decoder_1_out4, out=open
  // NOT_Gate not_7 has open pins: in=decoder_1_out5, out=open
  // NOT_Gate not_8 has open pins: in=decoder_1_out6, out=open
  // NOT_Gate not_9 has open pins: in=decoder_1_out7, out=open
  // NOT_Gate not_10 has open pins: in=decoder_1_out8, out=open
  not not_11 (not_11_out, decoder_1_out9);
  not not_12 (not_12_out, decoder_1_out10);
  // NOT_Gate not_13 has open pins: in=decoder_1_out11, out=open
  and and_1 (and_1_out, not_12_out, not_14_out);
  not not_14 (not_14_out, decoder_1_out12);
  not not_15 (not_15_out, decoder_1_out13);
  // NOT_Gate not_16 has open pins: in=decoder_1_out14, out=open
  // NOT_Gate not_17 has open pins: in=decoder_1_out15, out=open
  LED Q0 (.in(j_k_ff_1_q[0]));
  J_K_Flip_Flop j_k_ff_1 (
    .J(and_1_out), .clk(Reloj_out), .K(and_2_out), .Q(j_k_ff_1_q[0]), .en(1'b1), .reset(Reset_out));  // open: Qn, preset
  and and_2 (and_2_out, not_11_out, not_15_out);
endmodule
