// Logisim project examenlabo.circ as structural Verilog: 4 circuits, main circuit main
module main (
);

  wire button_1_out, button_2_out, clock_1_out, comparator_1_eq, subcircuito1_1_out_8, subcircuito2_1_out_6;
  wire [1:0] subcircuito2_1_q0;
  wire [3:0] subcircuito1_1_q0;

  Clock clock_1 (.out(clock_1_out));
  Button button_1 (.out(button_1_out));
  Button button_2 (.out(button_2_out));
  Subcircuito1 subcircuito1_1 (
    .RESET(button_1_out), .E(comparator_1_eq), .Q3(subcircuito1_1_q0[3]), .Q2(subcircuito1_1_q0[2]),
    .Q1(subcircuito1_1_q0[1]), .Q0(subcircuito1_1_q0[0]), .out_8(subcircuito1_1_out_8), .in_1(clock_1_out));
  LED led_1 (.in(subcircuito1_1_out_8));
  Subcircuito2 subcircuito2_1 (
    .RELOJ(clock_1_out), .RESET(button_2_out), .out_6(subcircuito2_1_out_6), .E(subcircuito1_1_out_8),
    .Q1(subcircuito2_1_q0[1]), .Q0(subcircuito2_1_q0[0]));
  LED led_2 (.in(subcircuito2_1_out_6));
  Hex_Digit_Display hex_digit_display_1 (.value(subcircuito1_1_q0));  // open: dp
  Hex_Digit_Display hex_digit_display_2 (.value({2'b00, subcircuito2_1_q0}));  // open: dp
  Comparator #(.width(4)) comparator_1 (
    .a(4'b0011), .b({2'b00, subcircuito2_1_q0}), .eq(comparator_1_eq));  // open: gt, lt

  // Notes on the sheet:
  //   Mi ID es:   02319455
  //   Mi secuencia es : 02319
endmodule

module Subcircuito1 (
  input  in_1,
  input  E,
  input  RESET,
  output Q3,
  output Q2,
  output Q1,
  output Q0,
  output out_8
);

  wire and_1_out, and_2_out, decoder_1_out0, decoder_1_out2, decoder_2_out3, multiplexer_1_out,
       multiplexer_2_out, not_1_out, not_2_out, or_1_out, xor_1_out;

  and and_1 (and_1_out, ~Q1, Q0, decoder_1_out0);  // AND_Gate
  Decoder #(.select(2), .enable("false")) decoder_1 (
    .out0(decoder_1_out0), .out2(decoder_1_out2), .sel({Q3, E}));  // open: out1, out3
  or or_1 (or_1_out, and_1_out, decoder_1_out2);
  Decoder #(.select(2), .enable("false")) decoder_2 (.out3(decoder_2_out3), .sel({Q3, E}));  // open: out0, out1, out2
  T_Flip_Flop T3 (.clk(in_1), .T(or_1_out), .Q(Q3), .reset(RESET));  // open: Qn, preset, en
  T_Flip_Flop T2 (.clk(in_1), .T(decoder_2_out3), .Q(Q2), .reset(RESET));  // open: Qn, preset, en
  not not_1 (not_1_out, Q0);
  and and_2 (and_2_out, not_1_out, not_2_out);
  not not_2 (not_2_out, E);
  Multiplexer #(.select(3), .enable("false")) multiplexer_1 (
    .in0(1'b0), .in1(1'b0), .in2(1'b1), .in3(1'b0), .in4(1'b0), .in5(1'b0), .in6(1'b0), .in7(1'b0),
    .out(multiplexer_1_out), .sel({Q2, Q3, E}));
  D_Flip_Flop D1 (.clk(in_1), .D(and_2_out), .Q(Q1), .reset(RESET));  // open: Qn, preset, en
  xor xor_1 (xor_1_out, Q0, Q1);
  Multiplexer #(.select(3), .enable("false")) multiplexer_2 (
    .in0(xor_1_out), .in1(1'b0), .in2(1'b0), .in3(1'b0), .in4(1'b0), .in5(1'b0), .in6(1'b0), .in7(1'b0),
    .out(multiplexer_2_out), .sel({Q2, Q3, E}));
  J_K_Flip_Flop J0__K0 (
    .J(multiplexer_2_out), .clk(in_1), .K(multiplexer_1_out), .Q(Q0), .reset(RESET));  // open: Qn, preset, en
  Hex_Digit_Display hex_digit_display_1 (.value({Q3, Q2, Q1, Q0}));  // open: dp
  or or_2 (out_8, E, Q3, Q2);
endmodule

module Subcircuito2 (
  input  E,
  input  RELOJ,
  input  RESET,
  output Q1,
  output Q0,
  output out_6
);

  wire multiplexer_1_out, multiplexer_2_out, not_1_out;

  Multiplexer #(.select(2), .enable("false")) multiplexer_1 (
    .in0(1'b0), .in1(1'b0), .in2(Q0), .in3(1'b0), .out(multiplexer_1_out), .sel({E, Q1}));
  not not_1 (not_1_out, Q0);
  and and_1 (out_6, Q0, Q1, E);
  T_Flip_Flop t_ff_1 (.clk(RELOJ), .T(multiplexer_1_out), .Q(Q1), .reset(RESET));  // open: Qn, preset, en
  Multiplexer #(.select(2), .enable("false")) multiplexer_2 (
    .in0(1'b0), .in1(1'b1), .in2(1'b0), .in3(not_1_out), .out(multiplexer_2_out), .sel({Q1, E}));
  T_Flip_Flop t_ff_2 (.clk(RELOJ), .T(multiplexer_2_out), .Q(Q0), .reset(RESET));  // open: Qn, preset, en
  Hex_Digit_Display hex_digit_display_1 (.value({2'b00, Q1, Q0}));  // open: dp
endmodule

module COND1 (
  input  E,
  input  Q3,
  input  Q2,
  input  Q1,
  input  Q0,
  output D1
);

  wire not_1_out, not_2_out;

  not not_1 (not_1_out, E);
  not not_2 (not_2_out, Q0);
  and and_1 (D1, not_1_out, not_2_out);
endmodule
