// Logisim project CastillejoBravo_Paula-sesion3.circ as structural Verilog
module semisumatorio (
  input  A0,
  input  B0,
  output A0___B0,
  output Acarreo
);

  xor xor_1 (A0___B0, A0, B0);
  and and_1 (Acarreo, A0, B0);
endmodule

module sumador_total (
  input  A,
  input  B,
  input  C,
  output out_4,
  output Acarreo
);

  wire semisumatorio_1_a0___b0, semisumatorio_1_acarreo, semisumatorio_2_acarreo;

  semisumatorio semisumatorio_1 (.A0(A), .B0(B), .A0___B0(semisumatorio_1_a0___b0), .Acarreo(semisumatorio_1_acarreo));
  semisumatorio semisumatorio_2 (
    .A0(semisumatorio_1_a0___b0), .B0(C), .A0___B0(out_4), .Acarreo(semisumatorio_2_acarreo));
  or or_1 (Acarreo, semisumatorio_2_acarreo, semisumatorio_1_acarreo);
endmodule

module sumador_de_4_bits (
  input  A0,
  input  A1,
  input  B0,
  input  B1,
  input  C0,
  input  C1,
  input  D0,
  input  D1,
  output out_9,
  output out_10,
  output out_11,
  output out_12,
  output out_13
);

  wire semisumatorio_1_acarreo, sumador_total_1_acarreo, sumador_total_2_acarreo;

  semisumatorio semisumatorio_1 (.A0(A0), .B0(A1), .A0___B0(out_9), .Acarreo(semisumatorio_1_acarreo));
  sumador_total sumador_total_1 (
    .A(B1), .B(B0), .C(semisumatorio_1_acarreo), .out_4(out_10), .Acarreo(sumador_total_1_acarreo));
  sumador_total sumador_total_2 (
    .A(C1), .B(C0), .C(sumador_total_1_acarreo), .out_4(out_11), .Acarreo(sumador_total_2_acarreo));
  sumador_total sumador_total_3 (.A(D1), .B(D0), .C(sumador_total_2_acarreo), .out_4(out_12), .Acarreo(out_13));
endmodule

module Complemento_a_uno (
  input  A0,
  input  A1,
  input  A2,
  input  A3,
  output out_5,
  output out_6,
  output out_7,
  output out_8
);

  not not_1 (out_5, A0);
  not not_2 (out_6, A1);
  not not_3 (out_7, A2);
  not not_4 (out_8, A3);
endmodule

module Complemento_a_dos (
  input  in_1,
  input  in_2,
  input  in_3,
  input  in_4,
  output out_5,
  output out_6,
  output out_7,
  output out_8,
  output out_9
);

  wire complemento_a_uno_1_out_5, complemento_a_uno_1_out_6, complemento_a_uno_1_out_7,
       complemento_a_uno_1_out_8;

  Complemento_a_uno complemento_a_uno_1 (
    .A0(in_1), .A1(in_2), .A2(in_3), .A3(in_4), .out_5(complemento_a_uno_1_out_5),
    .out_6(complemento_a_uno_1_out_6), .out_7(complemento_a_uno_1_out_7), .out_8(complemento_a_uno_1_out_8));
  sumador_de_4_bits sumador_de_4_bits_1 (
    .A0(complemento_a_uno_1_out_5), .A1(1'b1), .B0(complemento_a_uno_1_out_6), .B1(1'b0),
    .C0(complemento_a_uno_1_out_7), .C1(1'b0), .D0(complemento_a_uno_1_out_8), .D1(1'b0), .out_9(out_5),
    .out_10(out_6), .out_11(out_7), .out_12(out_8), .out_13(out_9));
endmodule

module Sumatorio_complemento_a_dos (
  input  A0,
  input  A1,
  input  A2,
  input  A3,
  input  B0,
  input  B1,
  input  B2,
  input  B3,
  output out_9,
  output out_10,
  output out_11,
  output out_12,
  output out_13
);

  wire minus_B_out_5, minus_B_out_6, minus_B_out_7, minus_B_out_8, minus_B_out_9, sumador_out_13;

  Complemento_a_dos minus_B (
    .in_1(B0), .in_2(B1), .in_3(B2), .in_4(B3), .out_5(minus_B_out_5), .out_6(minus_B_out_6),
    .out_7(minus_B_out_7), .out_8(minus_B_out_8), .out_9(minus_B_out_9));
  sumador_de_4_bits sumador (
    .A0(A0), .A1(minus_B_out_5), .B0(A1), .B1(minus_B_out_6), .C0(A2), .C1(minus_B_out_7), .D0(A3),
    .D1(minus_B_out_8), .out_9(out_9), .out_10(out_10), .out_11(out_11), .out_12(out_12),
    .out_13(sumador_out_13));
  or or_1 (out_13, sumador_out_13, minus_B_out_9);
endmodule
