// Logisim project CastillejoBravo_Paula-sesion4.circ as structural Verilog: 2 circuits, main circuit Suma_de_productos
module Suma_de_productos (
  input  A,
  input  B,
  input  C,
  input  a_2,
  output F,
  output G
);

  wire and_1_out, and_2_out, and_3_out, and_4_out, and_5_out, and_6_out, and_7_out, and_8_out, and_9_out,
       not_1_out, not_2_out, not_3_out, not_4_out, not_5_out, or_2_out, or_3_out;

  not not_1 (not_1_out, A);
  not not_2 (not_2_out, B);
  not not_3 (not_3_out, A);
  not not_4 (not_4_out, B);
  and and_1 (and_1_out, not_4_out, C);
  and and_2 (and_2_out, B, not_5_out);
  not not_5 (not_5_out, C);
  and and_3 (and_3_out, B, C);
  and and_4 (and_4_out, not_1_out, not_2_out);
  and and_5 (and_5_out, not_3_out, a_2);
  and and_6 (and_6_out, and_1_out, a_2);
  and and_7 (and_7_out, and_2_out, a_2);
  and and_8 (and_8_out, and_3_out, a_2);
  or or_1 (G, and_8_out, and_9_out);
  and and_9 (and_9_out, A, a_2);
  or or_2 (or_2_out, and_4_out, and_5_out);
  or or_3 (or_3_out, and_6_out, and_7_out);
  or or_4 (F, or_2_out, or_3_out);
endmodule

module Producto_de_sumas (
  input  A,
  input  B,
  input  C,
  input  a_2,
  output F,
  output G
);

  wire and_1_out, and_3_out, and_4_out, not_1_out, not_2_out, not_3_out, not_4_out, not_5_out, not_6_out,
       or_1_out, or_2_out, or_3_out, or_4_out, or_5_out, or_6_out, or_7_out, or_8_out;

  not not_1 (not_1_out, B);
  not not_2 (not_2_out, A);
  or or_1 (or_1_out, not_2_out, B);
  not not_3 (not_3_out, A);
  not not_4 (not_4_out, A);
  or or_2 (or_2_out, not_4_out, not_5_out);
  not not_5 (not_5_out, B);
  not not_6 (not_6_out, C);
  or or_3 (or_3_out, A, B);
  or or_4 (or_4_out, A, C);
  or or_5 (or_5_out, not_1_out, a_2);
  or or_6 (or_6_out, or_1_out, C);
  or or_7 (or_7_out, not_3_out, a_2);
  or or_8 (or_8_out, or_2_out, not_6_out);
  and and_1 (and_1_out, or_3_out, or_4_out);
  and and_2 (G, and_1_out, a_2);
  and and_3 (and_3_out, or_5_out, or_6_out);
  and and_4 (and_4_out, or_7_out, or_8_out);
  and and_5 (F, and_3_out, and_4_out);
endmodule
