// Logisim project CastillejoBravo_Paula-sesion6.circ as structural Verilog: 4 circuits, main circuit PUERTAS NAND suma de productos
module PUERTAS_NAND_suma_de_productos (
  input  A,
  input  B,
  input  C,
  output F
);

  wire nand_1_out, nand_2_out, nand_3_out, nand_4_out, nand_5_out, nand_6_out;

  nand nand_1 (nand_1_out, A, A);
  nand nand_2 (nand_2_out, B, B);
  nand nand_3 (nand_3_out, C, C);
  nand nand_4 (nand_4_out, A, A);
  nand nand_5 (nand_5_out, nand_1_out, nand_2_out, nand_3_out);
  nand nand_6 (nand_6_out, nand_4_out, B, C);
  nand nand_7 (F, nand_5_out, nand_6_out);
endmodule

module PUERTAS_NAND__productos_de_sumas (
  input  A,
  input  B,
  input  C,
  output F
);

  wire nand_1_out, nand_2_out, nand_3_out, nand_4_out, nand_5_out, nand_6_out;

  nand nand_1 (nand_1_out, B, B);
  nand nand_2 (nand_2_out, C, C);
  nand nand_3 (nand_3_out, nand_1_out, C);
  nand nand_4 (nand_4_out, B, nand_2_out);
  nand nand_5 (nand_5_out, A, A);
  nand nand_6 (nand_6_out, nand_3_out, nand_4_out, nand_5_out);
  nand nand_7 (F, nand_6_out, nand_6_out);
endmodule

module EXPRESION_SIMPLIFICADA_OR_AND (
  input  A,
  input  B,
  input  C,
  output F
);

  wire and_1_out, not_1_out, not_2_out, not_3_out, or_1_out, or_2_out;

  not not_1 (not_1_out, C);
  not not_2 (not_2_out, B);
  or or_1 (or_1_out, B, not_1_out);
  or or_2 (or_2_out, not_2_out, C);
  and and_1 (and_1_out, or_1_out, or_2_out);
  not not_3 (not_3_out, A);
  and and_2 (F, and_1_out, not_3_out);
endmodule

module FORMA_CANOCICA_1_AND_OR (
  input  A,
  input  B,
  input  C,
  output F
);

  wire and_1_out, and_2_out, and_3_out, and_4_out, not_1_out, not_2_out, not_3_out, not_4_out;

  not not_1 (not_1_out, A);
  not not_2 (not_2_out, B);
  not not_3 (not_3_out, A);
  and and_1 (and_1_out, not_1_out, not_2_out);
  not not_4 (not_4_out, C);
  and and_2 (and_2_out, not_3_out, B);
  and and_3 (and_3_out, and_1_out, not_4_out);
  and and_4 (and_4_out, and_2_out, C);
  or or_1 (F, and_3_out, and_4_out);
endmodule
