// Logisim project BLOQUE_COMBINACIONAL_2.circ as structural Verilog: 7 circuits, main circuit codificador
module codificador (
  input  in_1,
  input  in_2,
  output out_3,
  output [2:0] out_4,
  output [1:0] out_5,
  output out_6,
  output out_7,
  output [2:0] out_8,
  output out_9
);

  Priority_Encoder #(.select(2)) priority_encoder_1 (.out(out_5));  // open: in0, in1, in2, in3, gs, en_out, en_in
  Priority_Encoder priority_encoder_2 (
    .in0(1'b0), .in1(1'b0), .in2(1'b0), .in3(1'b1), .in4(1'b0), .in5(1'b0), .in6(1'b0), .in7(1'b0),
    .out(out_4), .en_in(in_1), .gs(out_6), .en_out(out_3));
  Priority_Encoder priority_encoder_3 (
    .in0(1'b0), .in1(1'b0), .in2(1'b0), .in3(1'b1), .in4(1'b0), .in5(1'b0), .in6(1'b1), .in7(1'b0),
    .out(out_8), .en_in(in_2), .gs(out_9), .en_out(out_7));
endmodule

module decodificador (
  input  C,
  input  B,
  input  A,
  input  [2:0] in_4,
  input  C_2,
  input  B_2,
  input  A_2,
  input  [3:0] in_8,
  input  C_3,
  input  B_3,
  input  A_3,
  input  C_4,
  input  B_4,
  input  A_4,
  output F,
  output out_16,
  output out_17,
  output out_18,
  output out_19,
  output out_20,
  output out_21,
  output out_22,
  output out_23,
  output out_24,
  output out_25,
  output out_26,
  output out_27,
  output out_28,
  output out_29,
  output out_30,
  output out_31,
  output out_32,
  output out_33,
  output out_34,
  output out_35,
  output out_36,
  output out_37,
  output out_38,
  output out_39,
  output out_40,
  output out_41,
  output out_42
);

  wire and_1_out, and_2_out, and_3_out, and_4_out, decoder_3_out0, decoder_3_out1, decoder_3_out2,
       decoder_3_out3, decoder_4_out0, decoder_4_out2, decoder_4_out5, decoder_4_out6, decoder_5_out0,
       decoder_5_out1, decoder_5_out2, decoder_5_out3, decoder_5_out4, decoder_5_out5, decoder_5_out6,
       decoder_5_out7, decoder_6_out0, decoder_6_out1, decoder_6_out2, decoder_6_out3, decoder_6_out4,
       decoder_6_out5, decoder_6_out6, decoder_6_out7, not_1_out, not_2_out, not_4_out, not_7_out, not_8_out,
       not_11_out, not_13_out, not_14_out, not_17_out;

  Decoder #(.select(3)) decoder_1 (
    .out0(out_16), .out1(out_17), .out2(out_18), .out3(out_19), .out4(out_20), .out5(out_21), .out6(out_22),
    .out7(out_23), .sel(in_4), .en(1'b1));
  Decoder #(.select(4)) decoder_2 (
    .out0(out_25), .out1(out_26), .out2(out_27), .out3(out_28), .out4(out_29), .out5(out_30), .out6(out_31),
    .out7(out_32), .out8(out_33), .out9(out_34), .out10(out_35), .out11(out_36), .out12(out_37),
    .out13(out_38), .out14(out_38), .out15(out_38), .sel(in_8), .en(1'b1));
  Decoder #(.select(2)) decoder_3 (
    .out0(decoder_3_out0), .out1(decoder_3_out1), .out2(decoder_3_out2), .out3(decoder_3_out3), .sel({A, B}),
    .en(1'b1));
  not not_1 (not_1_out, C);
  Decoder #(.select(3)) decoder_4 (
    .out0(decoder_4_out0), .out2(decoder_4_out2), .out5(decoder_4_out5), .out6(decoder_4_out6),
    .sel({A_2, B_2, C_2}), .en(1'b1));  // open: out1, out3, out4, out7
  not not_2 (not_2_out, decoder_5_out0);
  // NOT_Gate not_3 has open pins: in=decoder_5_out1, out=open
  not not_4 (not_4_out, decoder_5_out2);
  // NOT_Gate not_5 has open pins: in=decoder_5_out3, out=open
  // NOT_Gate not_6 has open pins: in=decoder_5_out4, out=open
  not not_7 (not_7_out, decoder_5_out5);
  not not_8 (not_8_out, decoder_5_out6);
  // NOT_Gate not_9 has open pins: in=decoder_5_out7, out=open
  Decoder #(.select(3)) decoder_5 (
    .out0(decoder_5_out0), .out1(decoder_5_out1), .out2(decoder_5_out2), .out3(decoder_5_out3),
    .out4(decoder_5_out4), .out5(decoder_5_out5), .out6(decoder_5_out6), .out7(decoder_5_out7),
    .sel({A_3, B_3, C_3}), .en(1'b1));
  // NOT_Gate not_10 has open pins: in=decoder_6_out0, out=open
  not not_11 (not_11_out, decoder_6_out1);
  // NOT_Gate not_12 has open pins: in=decoder_6_out2, out=open
  not not_13 (not_13_out, decoder_6_out3);
  not not_14 (not_14_out, decoder_6_out4);
  // NOT_Gate not_15 has open pins: in=decoder_6_out5, out=open
  // NOT_Gate not_16 has open pins: in=decoder_6_out6, out=open
  not not_17 (not_17_out, decoder_6_out7);
  Decoder #(.select(3)) decoder_6 (
    .out0(decoder_6_out0), .out1(decoder_6_out1), .out2(decoder_6_out2), .out3(decoder_6_out3),
    .out4(decoder_6_out4), .out5(decoder_6_out5), .out6(decoder_6_out6), .out7(decoder_6_out7),
    .sel({A_4, B_4, C_4}), .en(1'b1));
  and and_1 (and_1_out, not_1_out, decoder_3_out0);
  and and_2 (and_2_out, not_1_out, decoder_3_out1);
  and and_3 (and_3_out, C, decoder_3_out2);
  and and_4 (and_4_out, not_1_out, decoder_3_out3);
  or or_1 (out_24, decoder_4_out0, decoder_4_out2, decoder_4_out5, decoder_4_out6);
  or or_2 (F, and_1_out, and_2_out, and_3_out, and_4_out);
  nand nand_1 (out_41, not_2_out, not_4_out, not_7_out, not_8_out);
  and and_5 (out_42, not_11_out, not_13_out, not_14_out, not_17_out);

  assign out_39 = out_38;
  assign out_40 = out_38;
endmodule

module multiplexor (
  input  in_1,
  input  A,
  input  B,
  input  C,
  input  A_2,
  input  B_2,
  output out_7,
  output F,
  output out_9
);

  Multiplexer multiplexer_1 (.in0(1'b1), .in1(1'b0), .out(out_7), .sel(in_1), .en(1'b1));
  Multiplexer #(.select(3)) multiplexer_2 (
    .in0(1'b1), .in1(1'b0), .in2(1'b1), .in3(1'b0), .in4(1'b0), .in5(1'b1), .in6(1'b1), .in7(1'b0), .out(F),
    .sel({C, B, A}), .en(1'b1));
  Multiplexer #(.select(2)) multiplexer_3 (
    .in0(1'b1), .in1(1'b1), .in2(1'b0), .in3(1'b1), .out(out_9), .sel({B_2, A_2}), .en(1'b1));
endmodule

module demultiplexor (
  input  in_1,
  input  in_2,
  input  in_3,
  input  in_4,
  output out_5,
  output out_6,
  output out_7,
  output out_8
);

  Demultiplexer #(.select(2)) demultiplexer_1 (
    .out0(out_5), .out1(out_6), .out2(out_7), .out3(out_8), .in(in_1), .sel({in_4, in_3}), .en(in_2));
endmodule

module bloque_combinacional (
  input  A,
  input  B,
  input  C,
  input  D,
  output P,
  output Q,
  output R,
  output S
);

  wire and_1_out, and_2_out, and_3_out, and_4_out, and_5_out, and_6_out, and_7_out, not_1_out, not_2_out,
       not_3_out, not_4_out, not_5_out, not_6_out;

  and and_1 (and_1_out, B, D);
  and and_2 (and_2_out, B, C);
  not not_1 (not_1_out, B);
  and and_3 (and_3_out, not_1_out, D);
  not not_2 (not_2_out, B);
  and and_4 (and_4_out, not_2_out, C);
  and and_5 (and_5_out, B, not_3_out, not_4_out);
  not not_3 (not_3_out, C);
  not not_4 (not_4_out, D);
  not not_5 (not_5_out, C);
  and and_6 (and_6_out, not_5_out, not_6_out);
  not not_6 (not_6_out, D);
  and and_7 (and_7_out, C, D);
  not not_7 (S, D);
  or or_1 (P, and_1_out, and_2_out, A);
  or or_2 (Q, and_3_out, and_4_out, and_5_out);
  or or_3 (R, and_6_out, and_7_out);
  Hex_Digit_Display hex_digit_display_1 (.value({P, Q, R, S}));  // open: dp
endmodule

module bloque_combinacional_2 (
  input  D,
  input  C,
  input  B,
  input  in_4,
  input  A,
  output out_6
);

  wire or_1_out;

  or or_1 (or_1_out, D, C);
  Multiplexer #(.select(2)) multiplexer_1 (
    .in0(1'b0), .in1(or_1_out), .in2(1'b1), .in3(1'b1), .out(out_6), .sel({A, B}), .en(in_4));
endmodule

module Red_de_decodificadores_2x4 (
  input  c,
  input  B,
  input  A,
  output out_4
);

  wire decoder_1_out0, decoder_1_out2, decoder_2_out1, decoder_2_out2, not_1_out;

  not not_1 (not_1_out, A);
  Decoder #(.select(2)) decoder_1 (
    .out0(decoder_1_out0), .out2(decoder_1_out2), .sel({B, c}), .en(not_1_out));  // open: out1, out3
  Decoder #(.select(2)) decoder_2 (
    .out1(decoder_2_out1), .out2(decoder_2_out2), .sel({B, c}), .en(A));  // open: out0, out3
  or or_1 (out_4, decoder_1_out0, decoder_1_out2, decoder_2_out1, decoder_2_out2);
endmodule
