// Logisim project CastillejoBravo_Paula-sesion8.circ as structural Verilog: 3 circuits, main circuit Mux 4x1
module Mux_4x1 (
  input  C,
  input  D,
  input  B,
  input  A,
  output f
);

  wire and_1_out, not_1_out, not_2_out, xor_1_out;

  not not_1 (not_1_out, C);
  xor xor_1 (xor_1_out, C, D);
  not not_2 (not_2_out, D);
  and and_1 (and_1_out, not_1_out, D);
  Multiplexer #(.select(2)) multiplexer_1 (
    .in0(not_1_out), .in1(xor_1_out), .in2(and_1_out), .in3(not_2_out), .out(f), .sel({A, B}), .en(1'b1));
endmodule

module Dec_3x8 (
  input  D,
  input  A,
  input  B,
  input  C,
  output f
);

  wire and_1_out, and_2_out, and_3_out, and_4_out, and_5_out, and_6_out, decoder_1_out0, decoder_1_out2,
       decoder_1_out3, decoder_1_out4, decoder_1_out6, decoder_1_out7, not_1_out;

  Decoder #(.select(3)) decoder_1 (
    .out0(decoder_1_out0), .out2(decoder_1_out2), .out3(decoder_1_out3), .out4(decoder_1_out4),
    .out6(decoder_1_out6), .out7(decoder_1_out7), .sel({A, B, C}), .en(1'b1));  // open: out1, out5
  not not_1 (not_1_out, D);
  and and_1 (and_1_out, 1'b1, decoder_1_out0);
  and and_2 (and_2_out, D, decoder_1_out2);
  and and_3 (and_3_out, not_1_out, decoder_1_out3);
  and and_4 (and_4_out, D, decoder_1_out4);
  and and_5 (and_5_out, not_1_out, decoder_1_out6);
  and and_6 (and_6_out, not_1_out, decoder_1_out7);
  or or_1 (f, and_1_out, and_2_out, and_3_out, and_4_out, and_5_out, and_6_out);
endmodule

module Dec_4X16_NEGADO (
  input  A,
  input  B,
  input  C,
  input  D,
  output f
);

  wire decoder_1_out0, decoder_1_out1, decoder_1_out2, decoder_1_out3, decoder_1_out4, decoder_1_out5,
       decoder_1_out6, decoder_1_out7, decoder_1_out8, decoder_1_out9, decoder_1_out10, decoder_1_out11,
       decoder_1_out12, decoder_1_out13, decoder_1_out14, decoder_1_out15, not_3_out, not_4_out, not_5_out,
       not_8_out, not_9_out, not_11_out, not_12_out, not_14_out, not_16_out;

  // NOT_Gate not_1 has open pins: in=decoder_1_out0, out=open
  // NOT_Gate not_2 has open pins: in=decoder_1_out1, out=open
  not not_3 (not_3_out, decoder_1_out2);
  not not_4 (not_4_out, decoder_1_out3);
  not not_5 (not_5_out, decoder_1_out4);
  // NOT_Gate not_6 has open pins: in=decoder_1_out5, out=open
  // NOT_Gate not_7 has open pins: in=decoder_1_out6, out=open
  not not_8 (not_8_out, decoder_1_out7);
  not not_9 (not_9_out, decoder_1_out8);
  // NOT_Gate not_10 has open pins: in=decoder_1_out9, out=open
  not not_11 (not_11_out, decoder_1_out10);
  not not_12 (not_12_out, decoder_1_out11);
  // NOT_Gate not_13 has open pins: in=decoder_1_out12, out=open
  not not_14 (not_14_out, decoder_1_out13);
  // NOT_Gate not_15 has open pins: in=decoder_1_out14, out=open
  not not_16 (not_16_out, decoder_1_out15);
  Decoder #(.select(4)) decoder_1 (
    .out0(decoder_1_out0), .out1(decoder_1_out1), .out2(decoder_1_out2), .out3(decoder_1_out3),
    .out4(decoder_1_out4), .out5(decoder_1_out5), .out6(decoder_1_out6), .out7(decoder_1_out7),
    .out8(decoder_1_out8), .out9(decoder_1_out9), .out10(decoder_1_out10), .out11(decoder_1_out11),
    .out12(decoder_1_out12), .out13(decoder_1_out13), .out14(decoder_1_out14), .out15(decoder_1_out15),
    .sel({A, B, C, D}), .en(1'b1));
  and and_1 (f, not_3_out, not_4_out, not_5_out, not_8_out, not_9_out, not_11_out, not_12_out, not_14_out, not_16_out);
endmodule
