// Logisim project CastillejoBravo_Paula-sesion9.circ as structural Verilog: 3 circuits, main circuit Ejercicio 1
// CONTDOR 1
module Ejercicio_1 (
  input  RELOJ,
  input  PRESET,
  input  CLEAR,
  output S0,
  output S1
);

  wire button_1_out, button_2_out, j_k_ff_1_qn;

  J_K_Flip_Flop j_k_ff_1 (
    .J(1'b1), .clk(RELOJ), .K(1'b1), .Q(S0), .Qn(j_k_ff_1_qn), .preset(PRESET), .en(1'b1), .reset(CLEAR));
  Button button_1 (.out(button_1_out));
  J_K_Flip_Flop j_k_ff_2 (
    .J(1'b1), .clk(j_k_ff_1_qn), .K(1'b1), .Q(S1), .preset(button_1_out), .en(1'b1), .reset(button_2_out));  // open: Qn
  Button button_2 (.out(button_2_out));
  Hex_Digit_Display hex_digit_display_1 (.value({2'b00, S1, S0}));  // open: dp
endmodule

// CONTADOR 2
module Ejercicio_2 (
  input  RELOJ,
  input  PRESET,
  input  RESET,
  output S0,
  output S1
);

  wire button_1_out, button_2_out;

  J_K_Flip_Flop j_k_ff_1 (
    .J(1'b1), .clk(RELOJ), .K(1'b1), .Q(S0), .preset(PRESET), .en(1'b1), .reset(RESET));  // open: Qn
  Button button_1 (.out(button_1_out));
  J_K_Flip_Flop j_k_ff_2 (
    .J(1'b1), .clk(S0), .K(1'b1), .Q(S1), .preset(button_1_out), .en(1'b1), .reset(button_2_out));  // open: Qn
  Button button_2 (.out(button_2_out));
  Hex_Digit_Display hex_digit_display_1 (.value({2'b00, S1, S0}));  // open: dp

  // Notes on the sheet:
  //   LA CUENTA VA HACIA ATRÁS
endmodule

module Ejercicio_3 (
);

  wire CLEAR_2_out, CLEAR_out, clock_1_out, comparator_1_eq, PRESET_2_out, PRESET_out;
  wire [1:0] ejercicio_1_1_s0, ejercicio_2_1_s0;

  Clock clock_1 (.out(clock_1_out));
  Button PRESET (.out(PRESET_out));
  Button CLEAR (.out(CLEAR_out));
  Button PRESET_2 (.out(PRESET_2_out));
  Button CLEAR_2 (.out(CLEAR_2_out));
  Ejercicio_1 ejercicio_1_1 (
    .S0(ejercicio_1_1_s0[0]), .S1(ejercicio_1_1_s0[1]), .RELOJ(clock_1_out), .PRESET(PRESET_out),
    .CLEAR(CLEAR_out));
  Ejercicio_2 ejercicio_2_1 (
    .RELOJ(clock_1_out), .PRESET(PRESET_2_out), .S0(ejercicio_2_1_s0[0]), .S1(ejercicio_2_1_s0[1]),
    .RESET(CLEAR_2_out));
  Hex_Digit_Display hex_digit_display_1 (.value({2'b00, ejercicio_1_1_s0}));  // open: dp
  Hex_Digit_Display hex_digit_display_2 (.value({2'b00, ejercicio_2_1_s0}));  // open: dp
  Comparator #(.width(4)) comparator_1 (
    .a({2'b00, ejercicio_1_1_s0}), .b({2'b00, ejercicio_2_1_s0}), .eq(comparator_1_eq));  // open: gt, lt
  LED led_1 (.in(comparator_1_eq));
endmodule
